// Logisim project ORT2Project.circ as structural Verilog: 8 circuits, main circuit COMPUTER
module COMPUTER (
);

  wire BTN_INTR0_out, BTN_INTR1_out, BTN_INTR2_out, BTN_INTR3_out, BTN_INTR4_out, BTN_INTR5_out,
       BTN_INTR6_out, BTN_INTR7_out, BTN_RST_out, CLK, cpu_1_inta, pull_resistor_3_node,
       pull_resistor_5_node, ram_1_out_8, rst;
  wire [2:0] cpu_1_uext1__0;
  wire [7:0] interrupt_interface_8_1_intr7__0, pull_resistor_4_node, ram_1_out_7;
  wire [15:0] pull_resistor_1_node;

  Button BTN_RST (.out(BTN_RST_out));
  Clock u_CLK (.out(CLK));
  // RisingEdge risingedge_1: pin names not known; wires that end beside it: BTN_RST_out, CLK, rst
  RAM ram_1 (
    .in_1(pull_resistor_1_node), .in_2(CLK), .in_3(pull_resistor_4_node), .in_4(pull_resistor_3_node),
    .in_5(pull_resistor_5_node), .in_6(rst), .out_7(ram_1_out_7), .out_8(ram_1_out_8));
  Pull_Resistor pull_resistor_1 (.node(pull_resistor_1_node));
  Pull_Resistor pull_resistor_2 (.node(ram_1_out_7));
  Pull_Resistor pull_resistor_3 (.node(pull_resistor_3_node));
  Pull_Resistor pull_resistor_4 (.node(pull_resistor_4_node));
  Pull_Resistor pull_resistor_5 (.node(pull_resistor_5_node));
  Pull_Resistor pull_resistor_6 (.node(ram_1_out_8));
  CPU cpu_1 (
    .in_1(rst), .in_2(CLK), .in_3(ram_1_out_8), .in_4(ram_1_out_7), .ABUS(pull_resistor_1_node),
    .DOUTBUS(pull_resistor_4_node), .out_8(pull_resistor_3_node), .out_9(pull_resistor_5_node),
    .inta(cpu_1_inta), .intr3__0(interrupt_interface_8_1_intr7__0), .UEXT1__0(cpu_1_uext1__0));
  INTERRUPT_INTERFACE_8 interrupt_interface_8_1 (
    .BTN_INTR0(BTN_INTR0_out), .BTN_INTR1(BTN_INTR1_out), .BTN_INTR2(BTN_INTR2_out),
    .BTN_INTR3(BTN_INTR3_out), .BTN_INTR4(BTN_INTR4_out), .BTN_INTR5(BTN_INTR5_out),
    .BTN_INTR6(BTN_INTR6_out), .BTN_INTR7(BTN_INTR7_out), .inta(cpu_1_inta), .UEXT2__0(cpu_1_uext1__0),
    .CLK(CLK), .intr7__0(interrupt_interface_8_1_intr7__0));
  Button BTN_INTR7 (.out(BTN_INTR7_out));
  Button BTN_INTR6 (.out(BTN_INTR6_out));
  Button BTN_INTR5 (.out(BTN_INTR5_out));
  Button BTN_INTR4 (.out(BTN_INTR4_out));
  Button BTN_INTR3 (.out(BTN_INTR3_out));
  Button BTN_INTR2 (.out(BTN_INTR2_out));
  Button BTN_INTR1 (.out(BTN_INTR1_out));
  Button BTN_INTR0 (.out(BTN_INTR0_out));
endmodule

module CPU (
  input  in_1,
  input  in_2,
  input  in_3,
  input  [7:0] in_4,
  input  [7:0] intr3__0,
  output [15:0] ABUS,
  output [7:0] DOUTBUS,
  output out_8,
  output out_9,
  output inta,
  output [2:0] UEXT1__0
);

  wire PRENOS;
  wire [3:0] common_1_phaseffbus;
  wire [6:0] common_1_addrbus;
  wire [7:0] PSW, pull_resistor_1_node, pull_resistor_6_node;
  wire [8:0] pull_resistor_7_node;
  wire [14:0] pull_resistor_5_node;
  wire [15:0] ALU, B, INTRADDR, REGFILEOUT;
  wire [21:0] common_1_instrucbus;

  COMMON common_1 (
    .CLK(in_2), .RST(in_1), .DIN(in_4), .CMEMBUS(pull_resistor_5_node), .MAR(ABUS), .MDR(DOUTBUS),
    .PHASEFFBUS(common_1_phaseffbus), .INSTRUCBUS(common_1_instrucbus), .ADDRBUS(common_1_addrbus),
    .PSW(PSW), .CREGBUS(pull_resistor_7_node), .CFFBUS(pull_resistor_6_node), .B(B),
    .CPSW(pull_resistor_1_node), .ALU(ALU), .IVTPPDSP(INTRADDR), .REGFILEOUT(REGFILEOUT), .PRENOS(PRENOS));
  Pull_Resistor pull_resistor_1 (.node(pull_resistor_1_node));
  Pull_Resistor pull_resistor_2 (.node(common_1_instrucbus));
  Pull_Resistor pull_resistor_3 (.node(common_1_phaseffbus));
  Pull_Resistor pull_resistor_4 (.node(common_1_addrbus));
  Pull_Resistor pull_resistor_5 (.node(pull_resistor_5_node));
  Pull_Resistor pull_resistor_6 (.node(pull_resistor_6_node));
  Pull_Resistor pull_resistor_7 (.node(pull_resistor_7_node));
  FETCH fetch_1 (
    .in_2(in_1), .in_3(in_2), .in_4(in_3), .PHASEFFBUS(common_1_phaseffbus),
    .INSTRUCBUS(common_1_instrucbus), .ADDRBUS(common_1_addrbus), .PSW(PSW), .rdMEM(out_9),
    .CMEMBUS(pull_resistor_5_node), .CFFBUS(pull_resistor_6_node), .CREGBUS(pull_resistor_7_node));
  ADDR addr_1 (
    .in_1(in_1), .in_2(in_2), .in_3(in_3), .PHASEFFBUS(common_1_phaseffbus), .CMEMBUS(pull_resistor_5_node),
    .CFFBUS(pull_resistor_6_node), .CREGBUS(pull_resistor_7_node), .ADDRBUS(common_1_addrbus),
    .INSTRUCBUS(common_1_instrucbus), .rdMEM(out_9));
  EXEC exec_1 (
    .in_1(in_1), .in_2(in_2), .in_3(in_3), .B(B), .PHASEFFBUS(common_1_phaseffbus),
    .INSTRUCBUS(common_1_instrucbus), .ADDRBUS(common_1_addrbus), .PSW(PSW), .A(REGFILEOUT), .ALU(ALU),
    .CMEMBUS(pull_resistor_5_node), .CFFBUS(pull_resistor_6_node), .CREGBUS(pull_resistor_7_node),
    .CPSW(pull_resistor_1_node), .rdMEM(out_9), .wrMEM(out_8), .PRENOS(PRENOS));
  INTR intr_1 (
    .in_1(in_1), .in_2(in_2), .in_3(in_3), .PHASEFFBUS(common_1_phaseffbus),
    .INSTRUCBUS(common_1_instrucbus), .PSW(PSW), .intr(intr3__0), .ADDIVTP(INTRADDR),
    .CMEMBUS(pull_resistor_5_node), .CFFBUS(pull_resistor_6_node), .CREGBUS(pull_resistor_7_node),
    .rdMEM(out_9), .wrMEM(out_8), .UEXT1__0(UEXT1__0), .inta(inta));

  // Other names for the same wires on the sheet: CLK = in_2; DIN7__0[7:0] = in_4; FCBUS = in_3;
  //   intr7__0[7:0] = intr3__0; MAR[15:0] = ABUS; MDR[7:0] = DOUTBUS; RD = out_9; rst = in_1;
  //   UEXT2__0[2:0] = UEXT1__0; WR = out_8
endmodule

module COMMON (
  input  PRENOS,
  input  CLK,
  input  RST,
  input  [7:0] DIN,
  input  [15:0] ALU,
  input  [15:0] IVTPPDSP,
  input  [14:0] CMEMBUS,
  input  [7:0] CFFBUS,
  input  [8:0] CREGBUS,
  input  [7:0] CPSW,
  output [15:0] MAR,
  output [7:0] MDR,
  output [3:0] PHASEFFBUS,
  output [21:0] INSTRUCBUS,
  output [6:0] ADDRBUS,
  output [7:0] PSW,
  output [15:0] B,
  output [15:0] REGFILEOUT
);

  wire add16_1_p3, adr, and_1_out, and_2_out, and_6_out, and_7_out, and_8_out, and_9_out, and_10_out,
       and_11_out, and_12_out, and_13_out, and_14_out, and_15_out, and_16_out, and_17_out, and_18_out,
       and_19_out, and_20_out, and_21_out, and_22_out, and_23_out, and_24_out, and_25_out, and_26_out,
       and_27_out, and_28_out, and_30_out, bezadr, controlled_buffer_1_out, controlled_buffer_5_out,
       dc4_16_6_p3, dc4_16_6_p4, dc4_16_6_p5, ibs, ius, mp2_8b_1_p3, mp2_16b_1_p5, mp2_16b_2_p3, mp4_8b_1_p8,
       mp4_8b_2_p4, mp4_8b_3_p4, mp4_16b_1_p3, mp4_16b_2_p8, not_1_out, not_2_out, not_3_out, not_4_out,
       not_7_out, not_8_out, not_9_out, not_11_out, or_1_out, or_2_out, or_3_out, or_4_out, or_5_out,
       or_6_out, or_7_out, or_8_out, or_9_out, pull_resistor_2_node, rsff_2_p4, rsff_3_p4, rsff_4_p4,
       rsff_6_p4, rsff_6_p6, rsff_7_p4, rsff_8_p4, rsff_9_p3, rsff_9_p4, rsff_10_p3, rsff_10_p4;
  wire [3:0] check3, controlled_buffer_7_out, instrcheck;
  wire [7:0] check3_2, IR7__0, IR15__8, mp4_8b_2_p2, sub16_1_p2;
  wire [15:0] mp4_16b_1_p4;

  // ADD16 add16_1: pin names not known; wires that end beside it: {{9{IR15__8[7]}}, IR15__8[6:0]}, REGFILEOUT, add16_1_p3
  not not_1 (not_1_out, RST);
  // REG8_LD reg8_ld_1: pin names not known; wires that end beside it: CLK, not_1_out, MDR, {instrcheck, check3}, CREGBUS[3]
  // MP2_16b mp2_16b_1: pin names not known; wires that end beside it: IVTPPDSP, add16_1_p3, 1'b1, CREGBUS[8], mp2_16b_1_p5
  assign controlled_buffer_1_out = CREGBUS[7] ? 1'b0 : 1'bz;  // Controlled_Buffer controlled_buffer_1
  Pull_Resistor pull_resistor_1 (.node(controlled_buffer_1_out));
  // MP4_16b mp4_16b_1: pin names not known; wires that end beside it: 1'b1, {IR15__8, check3_2}, mp4_16b_1_p3, mp4_16b_1_p4, ALU, B, CREGBUS[5], CREGBUS[6]
  // ADD16 add16_2: pin names not known; wires that end beside it: REGFILEOUT, mp4_16b_1_p3, {{9{check3_2[7]}}, check3_2[6:0]}
  // DC4_16 dc4_16_1: pin names not known; wires that end beside it: instrcheck, PSW[0], bezadr, ius, ibs, adr
  // DC4_16 dc4_16_2: pin names not known; wires that end beside it: check3, ius, INSTRUCBUS[8], INSTRUCBUS[9], INSTRUCBUS[10], INSTRUCBUS[11], INSTRUCBUS[12], INSTRUCBUS[13]
  assign controlled_buffer_1_out = CMEMBUS[4] ? 1'b0 : 1'bz;  // Controlled_Buffer controlled_buffer_2
  // REG8_LD reg8_ld_2: pin names not known; wires that end beside it: CLK, not_1_out, MDR, check3_2, CREGBUS[2]
  assign controlled_buffer_1_out = CMEMBUS[3] ? 1'b1 : 1'bz;  // Controlled_Buffer controlled_buffer_3
  assign controlled_buffer_1_out = RST ? 1'b1 : 1'bz;  // Controlled_Buffer controlled_buffer_4
  // MP4_16b mp4_16b_2: pin names not known; wires that end beside it: mp2_16b_1_p5, B, {MDR, B[7:0]}, {IR7__0, IR15__8}, CMEMBUS[13], 1'b1, CMEMBUS[14], mp4_16b_2_p8
  assign controlled_buffer_5_out = CREGBUS[7] ? 1'b1 : 1'bz;  // Controlled_Buffer controlled_buffer_5
  Pull_Resistor pull_resistor_2 (.node(pull_resistor_2_node));
  assign pull_resistor_2_node = CMEMBUS[4] ? 1'b1 : 1'bz;  // Controlled_Buffer controlled_buffer_6
  assign controlled_buffer_7_out = CREGBUS[4] ? check3_2[3:0] : 4'bz;  // Controlled_Buffer controlled_buffer_7
  REG_FILE reg_file_1 (
    .DI(mp4_16b_1_p4), .Adress(controlled_buffer_7_out), .WR(controlled_buffer_1_out), .CLK(CLK),
    .DO(REGFILEOUT), .in_1(pull_resistor_2_node), .in_2(RST), .in_3(controlled_buffer_5_out));
  assign controlled_buffer_7_out = and_1_out ? CMEMBUS[8:5] : 4'bz;  // Controlled_Buffer controlled_buffer_8
  Pull_Resistor pull_resistor_3 (.node(CMEMBUS[13]));
  Pull_Resistor pull_resistor_4 (.node(CMEMBUS[14]));
  // MP2_16b mp2_16b_2: pin names not known; wires that end beside it: CMEMBUS[9], REGFILEOUT, mp2_16b_2_p3, mp4_16b_2_p8, 1'b1
  // REG16_INC_LD reg16_inc_ld_1: pin names not known; wires that end beside it: CLK, mp2_16b_2_p3, MAR, CMEMBUS[0], CMEMBUS[1]
  // REG8_LD reg8_ld_3: pin names not known; wires that end beside it: CLK, not_1_out, MDR, IR15__8, CREGBUS[1]
  // DC4_16 dc4_16_3: pin names not known; wires that end beside it: check3, bezadr, INSTRUCBUS[0], INSTRUCBUS[1], INSTRUCBUS[2], INSTRUCBUS[3], INSTRUCBUS[4], INSTRUCBUS[5], INSTRUCBUS[6], INSTRUCBUS[7]
  // DC4_16 dc4_16_4: pin names not known; wires that end beside it: check3, ibs, INSTRUCBUS[14], INSTRUCBUS[15], INSTRUCBUS[16]
  Pull_Resistor pull_resistor_5 (.node(controlled_buffer_5_out));
  not not_2 (not_2_out, RST);
  not not_3 (not_3_out, CREGBUS[4]);
  and and_1 (and_1_out, not_3_out, not_2_out);
  assign controlled_buffer_7_out = RST ? 4'b0010 : 4'bz;  // Controlled_Buffer controlled_buffer_9
  // MP4_8b mp4_8b_1: pin names not known; wires that end beside it: {3'b000, PSW[4:0]}, {PSW[5], {7{1'b0}}}, REGFILEOUT[7:0], REGFILEOUT[15:8], CMEMBUS[13], 1'b1, CMEMBUS[14], mp4_8b_1_p8
  // MP2_8b mp2_8b_1: pin names not known; wires that end beside it: CMEMBUS[10], DIN, mp2_8b_1_p3, mp4_8b_1_p8, 1'b1
  // REG8_LD reg8_ld_4: pin names not known; wires that end beside it: CLK, mp2_8b_1_p3, MDR, CMEMBUS[2]
  // REG8_LD reg8_ld_5: pin names not known; wires that end beside it: CLK, not_1_out, MDR, IR7__0, CREGBUS[0]
  // DC4_16 dc4_16_5: pin names not known; wires that end beside it: check3, adr, INSTRUCBUS[17], INSTRUCBUS[18], INSTRUCBUS[19], INSTRUCBUS[20], INSTRUCBUS[21]
  and and_2 (and_2_out, ~check3_2[0], ~check3_2[1], ~check3_2[2], ~check3_2[3]);  // AND_Gate
  // DC4_16 dc4_16_6: pin names not known; wires that end beside it: check3_2[7:4], adr, dc4_16_6_p3, dc4_16_6_p4, dc4_16_6_p5, ADDRBUS[3], ADDRBUS[4], ADDRBUS[5], ADDRBUS[6]
  and and_3 (ADDRBUS[0], and_2_out, dc4_16_6_p3);
  and and_4 (ADDRBUS[1], and_2_out, dc4_16_6_p4);
  not not_4 (not_4_out, RST);
  // RSFF rsff_1: pin names not known; wires that end beside it: CFFBUS[1], CLK, CFFBUS[0], not_4_out, PHASEFFBUS[0]
  and and_5 (ADDRBUS[2], and_2_out, dc4_16_6_p5);
  // MP4_8b mp4_8b_2: pin names not known; wires that end beside it: 1'b1, mp4_8b_2_p2, REGFILEOUT[15:8], mp4_8b_2_p4, MDR, IR7__0, CMEMBUS[14], CMEMBUS[13]
  // SUB16 sub16_1: pin names not known; wires that end beside it: 16'h2, {mp4_8b_2_p2, sub16_1_p2}, B
  // RSFF rsff_2: pin names not known; wires that end beside it: CFFBUS[3], CLK, CFFBUS[2], rsff_2_p4, PHASEFFBUS[1]
  not not_5 (rsff_2_p4, RST);
  // MP4_8b mp4_8b_3: pin names not known; wires that end beside it: 1'b1, sub16_1_p2, REGFILEOUT[7:0], mp4_8b_3_p4, MDR, IR15__8, CMEMBUS[14], CMEMBUS[13]
  // REG8_LD reg8_ld_6: pin names not known; wires that end beside it: CLK, mp4_8b_2_p4, B[15:8], CMEMBUS[11]
  // RSFF rsff_3: pin names not known; wires that end beside it: CFFBUS[5], CLK, CFFBUS[4], rsff_3_p4, PHASEFFBUS[2]
  not not_6 (rsff_3_p4, RST);
  and and_6 (and_6_out, ~REGFILEOUT[0], ~REGFILEOUT[1], ~REGFILEOUT[2], ~REGFILEOUT[3], ~REGFILEOUT[4], ~REGFILEOUT[5], ~REGFILEOUT[6], ~REGFILEOUT[7], ~REGFILEOUT[8], ~REGFILEOUT[9], ~REGFILEOUT[10], ~REGFILEOUT[11], ~REGFILEOUT[12], ~REGFILEOUT[13], ~REGFILEOUT[14], REGFILEOUT[15]);  // AND_Gate
  not not_7 (not_7_out, ALU[15]);
  not not_8 (not_8_out, B[15]);
  not not_9 (not_9_out, REGFILEOUT[15]);
  // REG8_LD reg8_ld_7: pin names not known; wires that end beside it: CLK, mp4_8b_3_p4, B[7:0], CMEMBUS[12]
  // RSFF rsff_4: pin names not known; wires that end beside it: CFFBUS[7], CLK, CFFBUS[6], rsff_4_p4, PHASEFFBUS[3]
  not not_10 (rsff_4_p4, RST);
  or or_1 (or_1_out, INSTRUCBUS[7], INSTRUCBUS[13], INSTRUCBUS[17], INSTRUCBUS[19], INSTRUCBUS[20], INSTRUCBUS[5]);
  or or_2 (or_2_out, INSTRUCBUS[7], INSTRUCBUS[13], INSTRUCBUS[17], INSTRUCBUS[19], INSTRUCBUS[20], INSTRUCBUS[21]);
  and and_7 (and_7_out, ~REGFILEOUT[0], ~REGFILEOUT[1], ~REGFILEOUT[2], ~REGFILEOUT[3], ~REGFILEOUT[4], ~REGFILEOUT[5], ~REGFILEOUT[6], ~REGFILEOUT[7], ~REGFILEOUT[9], ~REGFILEOUT[10], ~REGFILEOUT[11], ~REGFILEOUT[12], ~REGFILEOUT[13], ~REGFILEOUT[14], ~REGFILEOUT[15], ~REGFILEOUT[8]);  // AND_Gate
  and and_8 (and_8_out, not_7_out, B[15], REGFILEOUT[15]);
  and and_9 (and_9_out, ALU[15], not_8_out, not_9_out);
  and and_10 (and_10_out, MDR[2], INSTRUCBUS[2]);
  and and_11 (and_11_out, or_1_out, REGFILEOUT[15]);
  or or_3 (or_3_out, and_8_out, and_9_out);
  and and_12 (and_12_out, MDR[1], INSTRUCBUS[2]);
  and and_13 (and_13_out, or_2_out, and_7_out);
  or or_4 (or_4_out, and_10_out, and_11_out);
  and and_14 (and_14_out, INSTRUCBUS[13], and_6_out);
  and and_15 (and_15_out, MDR[3], INSTRUCBUS[2]);
  and and_16 (and_16_out, INSTRUCBUS[19], or_3_out);
  and and_17 (and_17_out, ~MDR[0], CPSW[6], INSTRUCBUS[2]);  // AND_Gate
  or or_5 (or_5_out, and_12_out, and_13_out);
  and and_18 (and_18_out, ~or_4_out, CPSW[1]);  // AND_Gate
  and and_19 (and_19_out, or_4_out, CPSW[1]);
  or or_6 (or_6_out, and_15_out, and_14_out, and_16_out);
  and and_20 (and_20_out, MDR[4], INSTRUCBUS[2]);
  and and_21 (and_21_out, INSTRUCBUS[19], PRENOS);
  and and_22 (and_22_out, MDR[7], INSTRUCBUS[2]);
  or or_7 (or_7_out, and_17_out, CPSW[0]);
  and and_23 (and_23_out, INSTRUCBUS[2], CPSW[6], MDR[0]);
  and and_24 (and_24_out, ~or_5_out, CPSW[2]);  // AND_Gate
  and and_25 (and_25_out, or_5_out, CPSW[2]);
  and and_26 (and_26_out, ~or_6_out, CPSW[4]);  // AND_Gate
  and and_27 (and_27_out, or_6_out, CPSW[4]);
  or or_8 (or_8_out, and_20_out, and_21_out);
  or or_9 (or_9_out, and_22_out, ~INSTRUCBUS[4], INSTRUCBUS[3]);  // OR_Gate
  not not_11 (not_11_out, RST);
  // RSFF rsff_5: pin names not known; wires that end beside it: or_7_out, CLK, and_23_out, not_11_out, PSW[0]
  // RSFF rsff_6: pin names not known; wires that end beside it: and_24_out, CLK, and_25_out, rsff_6_p4, rsff_6_p4, rsff_6_p6, PSW[1]
  not not_12 (rsff_6_p6, RST);
  // RSFF rsff_7: pin names not known; wires that end beside it: and_18_out, CLK, and_19_out, rsff_7_p4, PSW[2]
  not not_13 (rsff_7_p4, RST);
  // RSFF rsff_8: pin names not known; wires that end beside it: and_26_out, CLK, and_27_out, rsff_8_p4, PSW[3]
  and and_28 (and_28_out, ~or_8_out, CPSW[3]);  // AND_Gate
  // RSFF rsff_9: pin names not known; wires that end beside it: and_28_out, CLK, rsff_9_p3, rsff_9_p4, PSW[4]
  and and_29 (rsff_9_p3, or_8_out, CPSW[3]);
  and and_30 (and_30_out, ~or_9_out, CPSW[5]);  // AND_Gate
  // RSFF rsff_10: pin names not known; wires that end beside it: and_30_out, CLK, rsff_10_p3, rsff_10_p4, PSW[5]
  and and_31 (rsff_10_p3, or_9_out, CPSW[5]);
  not not_14 (rsff_8_p4, RST);
  not not_15 (rsff_9_p4, RST);
  not not_16 (rsff_10_p4, RST);

  // Other names for the same wires on the sheet: B7__0[7:0] = B[7:0]; B15__0[15:0] = B; MDR7__0[7:0] = MDR;
  //   IR23__16[7:0] = check3_2; immed = ADDRBUS[0]; memdir = ADDRBUS[1]; memind = ADDRBUS[2]; regind = ADDRBUS[3];
  //   regdir = ADDRBUS[4]; predec = ADDRBUS[5]; regindpom = ADDRBUS[6]; adresa[3:0] = CMEMBUS[8:5];
  //   ALU15__0[15:0] = ALU; B15__8[7:0] = B[15:8]; C = PRENOS; stFETCH = CFFBUS[0]; clFETCH = CFFBUS[1];
  //   stADDR = CFFBUS[2]; clADDR = CFFBUS[3]; stEXEC = CFFBUS[4]; clEXEC = CFFBUS[5]; stINTR = CFFBUS[6];
  //   clINTR = CFFBUS[7]; IR31__24[7:0] = {instrcheck, check3}; ldMAR = CMEMBUS[0]; incMAR = CMEMBUS[1];
  //   ldMDR = CMEMBUS[2]; ldPC = CMEMBUS[3]; incPC = CMEMBUS[4]; sMAR = CMEMBUS[9]; sMDR = CMEMBUS[10];
  //   ldB15__8 = CMEMBUS[11]; ldB7__0 = CMEMBUS[12]; BS1 = CMEMBUS[13]; BS0 = CMEMBUS[14]; clPSWSTART = CPSW[0];
  //   LDN = CPSW[1]; LDZ = CPSW[2]; LDC = CPSW[3]; LDV = CPSW[4]; LDI = CPSW[5]; PLDSTART = CPSW[6];
  //   ldIR7__0 = CREGBUS[0]; ldIR15__8 = CREGBUS[1]; ldIR23__16 = CREGBUS[2]; ldIR31__24 = CREGBUS[3];
  //   sIR19__16 = CREGBUS[4]; AS0 = CREGBUS[5]; AS1 = CREGBUS[6]; decPC = CREGBUS[7]; ISELECT = CREGBUS[8];
  //   Din7__0[7:0] = DIN; ENTRADDR15__0[15:0] = IVTPPDSP; HALT = INSTRUCBUS[0]; RTS = INSTRUCBUS[1];
  //   RTI = INSTRUCBUS[2]; INTE = INSTRUCBUS[3]; INTD = INSTRUCBUS[4]; ROL = INSTRUCBUS[5]; PUSH = INSTRUCBUS[6];
  //   POP = INSTRUCBUS[7]; BLEQ = INSTRUCBUS[8]; BNVF = INSTRUCBUS[9]; BLSSU = INSTRUCBUS[10]; BOVF = INSTRUCBUS[11];
  //   JEQL = INSTRUCBUS[12]; LOOPGRT = INSTRUCBUS[13]; BR = INSTRUCBUS[14]; JMP = INSTRUCBUS[15];
  //   JSR = INSTRUCBUS[16]; LD = INSTRUCBUS[17]; ST = INSTRUCBUS[18]; ADD = INSTRUCBUS[19]; NOT = INSTRUCBUS[20];
  //   MUL = INSTRUCBUS[21]; IR19__16[3:0] = check3_2[3:0]; MAR15__0[15:0] = MAR; FETCH = PHASEFFBUS[0];
  //   ADDR = PHASEFFBUS[1]; EXEC = PHASEFFBUS[2]; INTR = PHASEFFBUS[3]; PSW7__0[7:0] = PSW; PSWSTART = PSW[0];
  //   PSWZ = PSW[1]; PSWN = PSW[2]; PSWV = PSW[3]; PSWC = PSW[4]; PSWI = PSW[5]; BR7__0[7:0] = REGFILEOUT[7:0];
  //   REG_FILE_OUT[15:0] = REGFILEOUT; BR15__8[7:0] = REGFILEOUT[15:8]

  // Notes on the sheet:
  //   REGISTIRI OPSTE NAMENE
  //   MOZDA GRESKA
  //   Instrukcijski registar
  //   Dekoderi za prepoznavanje instrukcije na osnovu sadrzaja registra IR31..24
  //   MAR
  //   MDR
  //   MOZDA SE JAVI GRESKA
  //   FF za pokretanje FETCH, ADDR, EXEC i INTR faze izvršavanja instrukcije
  //   PRIHVATNI REGISTAR B
  //   Programska statusna reč (PSW)
endmodule

module FETCH (
  input  [3:0] PHASEFFBUS,
  input  in_2,
  input  in_3,
  input  in_4,
  input  [21:0] INSTRUCBUS,
  input  [6:0] ADDRBUS,
  input  [7:0] PSW,
  output [14:0] CMEMBUS,
  output [7:0] CFFBUS,
  output [8:0] CREGBUS,
  output rdMEM
);

  wire A1, adr, adr2, adr3, and_3_out, and_4_out, and_5_out, and_6_out, and_7_out, and_8_out, and_9_out,
       and_10_out, and_11_out, bezadr1, bradr2, bradr3, brbezadr1, brcnd, brgradr, brgrinst, brjmp2, brjmp3,
       brnotFCBUS, bruncnd, clFETCH, gradr, grinst, incPC, jmp2, jmp3, ldIR7__0, ldIR15__8, ldIR23__16,
       ldIR31__24, ldMAR, ldMDR, not_1_out, not_3_out, not_4_out, not_5_out, notPSWSTandFETCH, or_4_out,
       or_7_out, or_9_out, or_10_out, reg5_cl_inc_ld_1_p5, reg5_cl_inc_ld_1_p6, stADDR, stEXEC;
  wire [3:0] CC;
  wire [4:0] BA, reg5_cl_inc_ld_1_p4;
  wire [12:5] rom32x24_1_dout;

  not not_1 (not_1_out, in_2);
  // REG5_CL_INC_LD reg5_cl_inc_ld_1: pin names not known; wires that end beside it: in_3, not_1_out, BA, reg5_cl_inc_ld_1_p4, reg5_cl_inc_ld_1_p5, reg5_cl_inc_ld_1_p6
  not not_2 (reg5_cl_inc_ld_1_p6, reg5_cl_inc_ld_1_p5);
  ROM32x24 rom32x24_1 (
    .A4__0(reg5_cl_inc_ld_1_p4), .CS(1'b1),
    .DOUT({A1, ldMAR, incPC, ldMDR, ldIR31__24, ldIR23__16, ldIR15__8, ldIR7__0, clFETCH, stADDR, stEXEC, rom32x24_1_dout[12], CC, rom32x24_1_dout[7:5], BA}));
  or or_1 (reg5_cl_inc_ld_1_p5, brcnd, bruncnd);
  or or_2 (bezadr1, INSTRUCBUS[1], INSTRUCBUS[2], INSTRUCBUS[3], INSTRUCBUS[4], INSTRUCBUS[5], INSTRUCBUS[6], INSTRUCBUS[7], INSTRUCBUS[0]);
  or or_3 (jmp2, INSTRUCBUS[8], INSTRUCBUS[9], INSTRUCBUS[10], INSTRUCBUS[11], INSTRUCBUS[14]);
  // DC4_16 dc4_16_1: pin names not known; wires that end beside it: CC, 1'b1, bruncnd, notPSWSTandFETCH, brbezadr1, brjmp2, bradr2, brjmp3, bradr3, brnotFCBUS, brgrinst, brgradr
  or or_4 (or_4_out, ADDRBUS[3], ADDRBUS[4], ADDRBUS[5]);
  and and_1 (adr3, ADDRBUS[6], adr);
  and and_2 (adr2, or_4_out, adr);
  not not_3 (not_3_out, PSW[0]);
  not not_4 (not_4_out, PHASEFFBUS[0]);
  or or_5 (jmp3, INSTRUCBUS[12], INSTRUCBUS[13], INSTRUCBUS[15], INSTRUCBUS[16]);
  or or_6 (adr, INSTRUCBUS[17], INSTRUCBUS[18], INSTRUCBUS[19], INSTRUCBUS[20], INSTRUCBUS[21]);
  or or_7 (or_7_out, not_3_out, not_4_out);
  not not_5 (not_5_out, in_4);
  and and_3 (and_3_out, or_7_out, notPSWSTandFETCH);
  and and_4 (and_4_out, brbezadr1, bezadr1);
  and and_5 (and_5_out, brjmp2, jmp2);
  and and_6 (and_6_out, bradr2, adr2);
  and and_7 (and_7_out, brjmp3, jmp3);
  and and_8 (and_8_out, bradr3, adr3);
  and and_9 (and_9_out, brnotFCBUS, not_5_out);
  and and_10 (and_10_out, brgrinst, grinst);
  and and_11 (and_11_out, brgradr, gradr);
  or or_8 (brcnd, and_3_out, and_4_out, and_5_out, and_6_out, and_11_out, and_8_out, and_9_out, and_7_out, and_10_out);
  or or_9 (or_9_out, ADDRBUS[0], ADDRBUS[1], ADDRBUS[2], ADDRBUS[3], ADDRBUS[4], ADDRBUS[5], ADDRBUS[6]);
  nor nor_1 (grinst, INSTRUCBUS[0], INSTRUCBUS[1], INSTRUCBUS[2], INSTRUCBUS[3], INSTRUCBUS[4], INSTRUCBUS[5], INSTRUCBUS[6], INSTRUCBUS[7], INSTRUCBUS[8], INSTRUCBUS[9], INSTRUCBUS[10], INSTRUCBUS[11], INSTRUCBUS[12], INSTRUCBUS[13], INSTRUCBUS[14], INSTRUCBUS[15], INSTRUCBUS[16], adr);
  and and_12 (gradr, ~or_9_out, adr);  // AND_Gate
  assign CMEMBUS[0] = ldMAR ? 1'b1 : 1'bz;  // Controlled_Buffer controlled_buffer_1
  assign CMEMBUS[2] = ldMDR ? 1'b1 : 1'bz;  // Controlled_Buffer controlled_buffer_2
  assign CMEMBUS[4] = incPC ? 1'b1 : 1'bz;  // Controlled_Buffer controlled_buffer_3
  assign CFFBUS[1] = clFETCH ? 1'b1 : 1'bz;  // Controlled_Buffer controlled_buffer_4
  assign CFFBUS[2] = stADDR ? 1'b1 : 1'bz;  // Controlled_Buffer controlled_buffer_5
  assign CFFBUS[4] = stEXEC ? 1'b1 : 1'bz;  // Controlled_Buffer controlled_buffer_6
  assign CMEMBUS[5] = A1 ? 1'b0 : 1'bz;  // Controlled_Buffer controlled_buffer_7
  assign CMEMBUS[6] = A1 ? A1 : 1'bz;  // Controlled_Buffer controlled_buffer_8
  assign CMEMBUS[7] = A1 ? 1'b0 : 1'bz;  // Controlled_Buffer controlled_buffer_9
  assign CMEMBUS[8] = A1 ? 1'b0 : 1'bz;  // Controlled_Buffer controlled_buffer_10
  assign CREGBUS[0] = ldIR7__0 ? 1'b1 : 1'bz;  // Controlled_Buffer controlled_buffer_11
  assign CREGBUS[1] = ldIR15__8 ? 1'b1 : 1'bz;  // Controlled_Buffer controlled_buffer_12
  assign CREGBUS[2] = ldIR23__16 ? 1'b1 : 1'bz;  // Controlled_Buffer controlled_buffer_13
  assign CREGBUS[3] = ldIR31__24 ? 1'b1 : 1'bz;  // Controlled_Buffer controlled_buffer_14
  or or_10 (or_10_out, ldMDR, ldMAR);
  assign rdMEM = or_10_out ? 1'b1 : 1'bz;  // Controlled_Buffer controlled_buffer_15

  // Other names for the same wires on the sheet: immed = ADDRBUS[0]; memdir = ADDRBUS[1]; memind = ADDRBUS[2];
  //   regind = ADDRBUS[3]; regdir = ADDRBUS[4]; predec = ADDRBUS[5]; regindpom = ADDRBUS[6]; CLK = in_3; FCBUS = in_4;
  //   HALT = INSTRUCBUS[0]; RTS = INSTRUCBUS[1]; RTI = INSTRUCBUS[2]; INTE = INSTRUCBUS[3]; INTD = INSTRUCBUS[4];
  //   ROL = INSTRUCBUS[5]; PUSH = INSTRUCBUS[6]; POP = INSTRUCBUS[7]; BLEQ = INSTRUCBUS[8]; BNVF = INSTRUCBUS[9];
  //   BLSSU = INSTRUCBUS[10]; BOVF = INSTRUCBUS[11]; JEQL = INSTRUCBUS[12]; LOOPGRT = INSTRUCBUS[13];
  //   BR = INSTRUCBUS[14]; JMP = INSTRUCBUS[15]; JSR = INSTRUCBUS[16]; LD = INSTRUCBUS[17]; ST = INSTRUCBUS[18];
  //   ADD = INSTRUCBUS[19]; NOT = INSTRUCBUS[20]; MUL = INSTRUCBUS[21]; FETCH = PHASEFFBUS[0]; ADDR = PHASEFFBUS[1];
  //   EXEC = PHASEFFBUS[2]; INTR = PHASEFFBUS[3]; PSWSTART = PSW[0]; rst = in_2

  // Notes on the sheet:
  //   Operaciona jedinica
  //   Kontrolna jedinica
endmodule

module ADDR (
  input  in_1,
  input  in_2,
  input  in_3,
  input  [3:0] PHASEFFBUS,
  input  [21:0] INSTRUCBUS,
  input  [6:0] ADDRBUS,
  output [14:0] CMEMBUS,
  output [7:0] CFFBUS,
  output [8:0] CREGBUS,
  output rdMEM
);

  wire and_1_out, and_2_out, and_3_out, bradr, brcnd, brnotADDR, brnotFCBUS, brSTORE, bruncd, BS0, BS1,
       clADDR, incMAR, ldB7__0, ldB15__8, ldMAR, ldMDR, ldPC, not_1_out, not_2_out, not_3_out, or_3_out,
       reg5_cl_inc_ld_1_p5, reg5_cl_inc_ld_1_p6, sIR19__16, sMAR, stEXEC;
  wire [3:0] CC;
  wire [4:0] reg5_cl_inc_ld_1_p4;
  wire [7:0] BA, mp2_8b_1_p3, mp2_8b_1_p4;

  not not_1 (not_1_out, PHASEFFBUS[1]);
  and and_1 (and_1_out, not_1_out, brnotADDR);
  and and_2 (and_2_out, brSTORE, INSTRUCBUS[18]);
  and and_3 (and_3_out, brnotFCBUS, not_2_out);
  not not_2 (not_2_out, in_3);
  or or_1 (brcnd, and_1_out, and_2_out, and_3_out);
  // MP2_8b mp2_8b_1: pin names not known; wires that end beside it: bradr, BA, mp2_8b_1_p3, mp2_8b_1_p4, 1'b1
  not not_3 (not_3_out, in_1);
  // REG5_CL_INC_LD reg5_cl_inc_ld_1: pin names not known; wires that end beside it: in_2, not_3_out, mp2_8b_1_p3[4:0], reg5_cl_inc_ld_1_p4, reg5_cl_inc_ld_1_p5, reg5_cl_inc_ld_1_p6
  KMADR kmadr_1 (
    .immed(ADDRBUS[0]), .memdir(ADDRBUS[1]), .regdir(ADDRBUS[4]), .regindpom(ADDRBUS[6]),
    .Adr7__0(mp2_8b_1_p4), .regind(ADDRBUS[3]), .memind(ADDRBUS[2]), .predec(ADDRBUS[5]));
  not not_4 (reg5_cl_inc_ld_1_p6, reg5_cl_inc_ld_1_p5);
  ROM32x24_ADDR rom32x24_addr_1 (
    .A4__0(reg5_cl_inc_ld_1_p4), .CS(1'b1),
    .DOUT({ldB15__8, ldB7__0, ldMAR, sMAR, ldMDR, BS0, BS1, incMAR, sIR19__16, ldPC, stEXEC, clADDR, CC, BA}));
  // DC4_16 dc4_16_1: pin names not known; wires that end beside it: CC, 1'b1, bruncd, brnotADDR, brSTORE, bradr, brnotFCBUS
  or or_2 (reg5_cl_inc_ld_1_p5, brcnd, bruncd, bradr);
  assign CMEMBUS[3] = ldPC ? 1'b1 : 1'bz;  // Controlled_Buffer controlled_buffer_1
  assign CMEMBUS[1] = incMAR ? 1'b1 : 1'bz;  // Controlled_Buffer controlled_buffer_2
  assign CMEMBUS[2] = ldMDR ? 1'b1 : 1'bz;  // Controlled_Buffer controlled_buffer_3
  assign CMEMBUS[9] = sMAR ? 1'b1 : 1'bz;  // Controlled_Buffer controlled_buffer_4
  assign CMEMBUS[11] = ldB15__8 ? 1'b1 : 1'bz;  // Controlled_Buffer controlled_buffer_5
  assign CMEMBUS[12] = ldB7__0 ? 1'b1 : 1'bz;  // Controlled_Buffer controlled_buffer_6
  assign CMEMBUS[13] = BS1 ? 1'b1 : 1'bz;  // Controlled_Buffer controlled_buffer_7
  assign CMEMBUS[14] = BS0 ? 1'b1 : 1'bz;  // Controlled_Buffer controlled_buffer_8
  assign CREGBUS[4] = sIR19__16 ? 1'b1 : 1'bz;  // Controlled_Buffer controlled_buffer_9
  assign CFFBUS[3] = clADDR ? 1'b1 : 1'bz;  // Controlled_Buffer controlled_buffer_10
  assign CFFBUS[4] = stEXEC ? 1'b1 : 1'bz;  // Controlled_Buffer controlled_buffer_11
  or or_3 (or_3_out, ldMDR, ldMAR);
  assign rdMEM = or_3_out ? 1'b1 : 1'bz;  // Controlled_Buffer controlled_buffer_12
  assign CMEMBUS[0] = ldMAR ? 1'b1 : 1'bz;  // Controlled_Buffer controlled_buffer_13

  // Other names for the same wires on the sheet: immed = ADDRBUS[0]; memdir = ADDRBUS[1]; memind = ADDRBUS[2];
  //   regind = ADDRBUS[3]; regdir = ADDRBUS[4]; predec = ADDRBUS[5]; regindpom = ADDRBUS[6]; CLK = in_2; FCBUS = in_3;
  //   HALT = INSTRUCBUS[0]; RTS = INSTRUCBUS[1]; RTI = INSTRUCBUS[2]; INTE = INSTRUCBUS[3]; INTD = INSTRUCBUS[4];
  //   ROL = INSTRUCBUS[5]; PUSH = INSTRUCBUS[6]; POP = INSTRUCBUS[7]; BLEQ = INSTRUCBUS[8]; BNVF = INSTRUCBUS[9];
  //   BLSSU = INSTRUCBUS[10]; BOVF = INSTRUCBUS[11]; JEQL = INSTRUCBUS[12]; LOOPGRT = INSTRUCBUS[13];
  //   BR = INSTRUCBUS[14]; JMP = INSTRUCBUS[15]; JSR = INSTRUCBUS[16]; LD = INSTRUCBUS[17]; ST = INSTRUCBUS[18];
  //   ADD = INSTRUCBUS[19]; NOT = INSTRUCBUS[20]; MUL = INSTRUCBUS[21]; FETCH = PHASEFFBUS[0]; ADDR = PHASEFFBUS[1];
  //   EXEC = PHASEFFBUS[2]; INTR = PHASEFFBUS[3]; rst = in_1

  // Notes on the sheet:
  //   Upravljacka jedinica
endmodule

module EXEC (
  input  in_1,
  input  in_2,
  input  in_3,
  input  [15:0] B,
  input  [15:0] A,
  input  [3:0] PHASEFFBUS,
  input  [21:0] INSTRUCBUS,
  input  [6:0] ADDRBUS,
  input  [7:0] PSW,
  output [15:0] ALU,
  output [14:0] CMEMBUS,
  output PRENOS,
  output [7:0] CFFBUS,
  output [8:0] CREGBUS,
  output [7:0] CPSW,
  output rdMEM,
  output wrMEM
);

  wire add16_2_p2, and_1_out, and_2_out, and_3_out, and_4_out, and_5_out, and_6_out, and_8_out, and_9_out,
       and_10_out, and_11_out, and_12_out, AS0, AS1, brcase, brcnd, brimmed, brnotbrorjmp, brnotexec,
       brnotfcbus, brorjmp, brregdir, bruncnd, BS0, BS1, clEXEC, clPSWSTART, decPC, incMAR, incPC, ldB7__0,
       ldB15__8, LDC, LDI, ldMAR, ldMDR, LDN, ldPC, LDPOSEBAN, LDV, LDZ, mp2_8b_1_p3, not_1_out, not_4_out,
       not_5_out, not_6_out, not_7_out, or_1_out, or_2_out, PLDSTART, reg8_inc_ld_1_p5, reg8_inc_ld_1_p6,
       SAS0, SAS1, SHIFT, sIR19__16, sMDR, stINTR, wrMEM_t, xor_1_out, xor_2_out;
  wire [2:0] CC;
  wire [3:0] adresa;
  wire [3:3] rom_exec_1_out_3;
  wire [7:0] kmopr_1_adr7__0, mp2_8b_1_p2, reg8_inc_ld_1_p4;
  wire [14:0] reg16_1_p4_2;
  wire [15:0] add16_1_p3, add16_2_p3, and_7_out, not_3_out, reg16_2_p4;
  wire [15:15] reg16_1_p4;

  assign ALU = INSTRUCBUS[5] ? {A[14:0], A[15]} : 16'bz;  // Controlled_Buffer controlled_buffer_1
  Pull_Resistor pull_resistor_1 (.node(ALU));
  xor xor_1 (xor_1_out, PSW[2], PSW[3]);
  or or_1 (or_1_out, xor_1_out, PSW[1]);
  // ADD16 add16_1: pin names not known; wires that end beside it: PRENOS, A, add16_1_p3, B
  assign ALU = INSTRUCBUS[19] ? add16_1_p3 : 16'bz;  // Controlled_Buffer controlled_buffer_2
  and and_1 (and_1_out, INSTRUCBUS[8], or_1_out);
  and and_2 (and_2_out, INSTRUCBUS[9], ~PSW[3]);  // AND_Gate
  and and_3 (and_3_out, INSTRUCBUS[10], PSW[4]);
  and and_4 (and_4_out, INSTRUCBUS[11], PSW[3]);
  and and_5 (and_5_out, INSTRUCBUS[12], PSW[1]);
  KMOPR kmopr_1 (
    .LD(INSTRUCBUS[17]), .ST(INSTRUCBUS[18]), .ADD(INSTRUCBUS[19]), .PUSH(INSTRUCBUS[6]),
    .BLSSU(INSTRUCBUS[10]), .JEQL(INSTRUCBUS[12]), .JMP(INSTRUCBUS[15]), .JSR(INSTRUCBUS[16]),
    .RTS(INSTRUCBUS[1]), .RTI(INSTRUCBUS[2]), .HALT(INSTRUCBUS[0]), .Adr7__0(kmopr_1_adr7__0),
    .INTE(INSTRUCBUS[3]), .INTD(INSTRUCBUS[4]), .ROL(INSTRUCBUS[5]), .BR(INSTRUCBUS[14]),
    .POP(INSTRUCBUS[7]), .BLEQ(INSTRUCBUS[8]), .BNVF(INSTRUCBUS[9]), .BOVF(INSTRUCBUS[11]),
    .LOOPGRT(INSTRUCBUS[13]), .NOT(INSTRUCBUS[20]), .MUL(INSTRUCBUS[21]));
  // MP2_8b mp2_8b_1: pin names not known; wires that end beside it: brcase, mp2_8b_1_p2, mp2_8b_1_p3, kmopr_1_adr7__0, 1'b1
  not not_1 (not_1_out, in_1);
  // REG8_INC_LD reg8_inc_ld_1: pin names not known; wires that end beside it: in_2, not_1_out, mp2_8b_1_p3, reg8_inc_ld_1_p4, reg8_inc_ld_1_p5, reg8_inc_ld_1_p6
  not not_2 (reg8_inc_ld_1_p6, reg8_inc_ld_1_p5);
  assign not_3_out = ~B;  // NOT_Gate not_3, 16 bits wide
  assign ALU = INSTRUCBUS[20] ? not_3_out : 16'bz;  // Controlled_Buffer controlled_buffer_3
  or or_2 (or_2_out, xor_2_out, PSW[1]);
  xor xor_2 (xor_2_out, PSW[2], PSW[3]);
  or or_3 (reg8_inc_ld_1_p5, brcase, brcnd, bruncnd);
  ROM_EXEC rom_exec_1 (
    .ADRESA(reg8_inc_ld_1_p4), .CS(1'b1), .out_4(mp2_8b_1_p2),
    .out_3({stINTR, BS1, incMAR, clPSWSTART, SAS0, decPC, ldMAR, ldMDR, ldB15__8, ldB7__0, BS0, ldPC, SAS1, LDC, LDV, LDN, LDZ, PLDSTART, LDI, AS0, AS1, incPC, sMDR, wrMEM_t, sIR19__16, LDPOSEBAN, SHIFT, clEXEC, rom_exec_1_out_3[3], CC}));
  and and_6 (and_6_out, ~or_2_out, INSTRUCBUS[13]);  // AND_Gate
  assign ALU = INSTRUCBUS[21] ? add16_2_p3 : 16'bz;  // Controlled_Buffer controlled_buffer_4
  or or_4 (brorjmp, and_3_out, and_1_out, and_2_out, and_4_out, and_5_out, and_6_out);
  // REG16 reg16_1: pin names not known; wires that end beside it: SHIFT, in_2, B, {reg16_1_p4_2, reg16_1_p4[15]}, LDPOSEBAN
  assign and_7_out = {16{reg16_1_p4[15]}} & reg16_2_p4;  // AND_Gate and_7, 16 bits wide
  // ADD16 add16_2: pin names not known; wires that end beside it: and_7_out, add16_2_p2, add16_2_p3
  not not_4 (not_4_out, in_1);
  // REG16_LD reg16_ld_1: pin names not known; wires that end beside it: in_2, not_4_out, add16_2_p2, add16_2_p3, SHIFT
  // REG16 reg16_2: pin names not known; wires that end beside it: 1'b0, in_2, A, reg16_2_p4, LDPOSEBAN, SHIFT, 1'b0
  not not_5 (not_5_out, PHASEFFBUS[2]);
  not not_6 (not_6_out, in_3);
  not not_7 (not_7_out, brorjmp);
  and and_8 (and_8_out, brnotexec, not_5_out);
  and and_9 (and_9_out, brnotfcbus, not_6_out);
  and and_10 (and_10_out, brnotbrorjmp, not_7_out);
  and and_11 (and_11_out, brimmed, ADDRBUS[0]);
  and and_12 (and_12_out, brregdir, ADDRBUS[4]);
  or or_5 (brcnd, and_8_out, and_9_out, and_10_out, and_11_out, and_12_out);
  // DC3_8 dc3_8_1: pin names not known; wires that end beside it: CC, 1'b1, bruncnd, brcase, brnotfcbus, brnotexec, brnotbrorjmp, brimmed, brregdir
  // MP4_4b mp4_4b_1: pin names not known; wires that end beside it: SAS1, SAS0, 4'b0000, 4'b0001, adresa, 4'b0010, 1'b1
  assign CMEMBUS[0] = ldMAR ? 1'b1 : 1'bz;  // Controlled_Buffer controlled_buffer_5
  assign CMEMBUS[1] = incMAR ? 1'b1 : 1'bz;  // Controlled_Buffer controlled_buffer_6
  assign CMEMBUS[2] = ldMDR ? 1'b1 : 1'bz;  // Controlled_Buffer controlled_buffer_7
  assign CMEMBUS[3] = ldPC ? 1'b1 : 1'bz;  // Controlled_Buffer controlled_buffer_8
  assign CMEMBUS[4] = incPC ? 1'b1 : 1'bz;  // Controlled_Buffer controlled_buffer_9
  assign CMEMBUS[10] = sMDR ? 1'b1 : 1'bz;  // Controlled_Buffer controlled_buffer_10
  assign CMEMBUS[11] = ldB15__8 ? 1'b1 : 1'bz;  // Controlled_Buffer controlled_buffer_11
  assign CMEMBUS[12] = ldB7__0 ? 1'b1 : 1'bz;  // Controlled_Buffer controlled_buffer_12
  assign CMEMBUS[13] = BS1 ? 1'b1 : 1'bz;  // Controlled_Buffer controlled_buffer_13
  assign CMEMBUS[14] = BS0 ? 1'b1 : 1'bz;  // Controlled_Buffer controlled_buffer_14
  assign CFFBUS[5] = clEXEC ? 1'b1 : 1'bz;  // Controlled_Buffer controlled_buffer_15
  assign CFFBUS[6] = stINTR ? 1'b1 : 1'bz;  // Controlled_Buffer controlled_buffer_16
  assign CREGBUS[4] = sIR19__16 ? 1'b1 : 1'bz;  // Controlled_Buffer controlled_buffer_17
  assign CREGBUS[5] = AS0 ? 1'b1 : 1'bz;  // Controlled_Buffer controlled_buffer_18
  assign CREGBUS[6] = AS1 ? 1'b1 : 1'bz;  // Controlled_Buffer controlled_buffer_19
  assign CPSW[0] = clPSWSTART ? 1'b1 : 1'bz;  // Controlled_Buffer controlled_buffer_20
  assign CPSW[1] = LDN ? 1'b1 : 1'bz;  // Controlled_Buffer controlled_buffer_21
  assign CPSW[2] = LDZ ? 1'b1 : 1'bz;  // Controlled_Buffer controlled_buffer_22
  assign CPSW[3] = LDC ? 1'b1 : 1'bz;  // Controlled_Buffer controlled_buffer_23
  assign CPSW[4] = LDV ? 1'b1 : 1'bz;  // Controlled_Buffer controlled_buffer_24
  assign CPSW[5] = LDI ? 1'b1 : 1'bz;  // Controlled_Buffer controlled_buffer_25
  assign CPSW[6] = PLDSTART ? 1'b1 : 1'bz;  // Controlled_Buffer controlled_buffer_26
  assign CMEMBUS[8:5] = PHASEFFBUS[2] ? adresa : 4'bz;  // Controlled_Buffer controlled_buffer_27
  assign CREGBUS[7] = decPC ? 1'b1 : 1'bz;  // Controlled_Buffer controlled_buffer_28
  assign wrMEM = wrMEM_t ? 1'b1 : 1'bz;  // Controlled_Buffer controlled_buffer_29

  // Other names for the same wires on the sheet: REGFILEOUT[15:0] = A; immed = ADDRBUS[0]; memdir = ADDRBUS[1];
  //   memind = ADDRBUS[2]; regind = ADDRBUS[3]; regdir = ADDRBUS[4]; predec = ADDRBUS[5]; regindpom = ADDRBUS[6];
  //   ALU15__0[15:0] = ALU; B15__0[15:0] = B; C = PRENOS; CLK = in_2; FCBUS = in_3; HALT = INSTRUCBUS[0];
  //   RTS = INSTRUCBUS[1]; RTI = INSTRUCBUS[2]; INTE = INSTRUCBUS[3]; INTD = INSTRUCBUS[4]; ROL = INSTRUCBUS[5];
  //   PUSH = INSTRUCBUS[6]; POP = INSTRUCBUS[7]; BLEQ = INSTRUCBUS[8]; BNVF = INSTRUCBUS[9]; BLSSU = INSTRUCBUS[10];
  //   BOVF = INSTRUCBUS[11]; JEQL = INSTRUCBUS[12]; LOOPGRT = INSTRUCBUS[13]; BR = INSTRUCBUS[14];
  //   JMP = INSTRUCBUS[15]; JSR = INSTRUCBUS[16]; LD = INSTRUCBUS[17]; ST = INSTRUCBUS[18]; ADD = INSTRUCBUS[19];
  //   NOT = INSTRUCBUS[20]; MUL = INSTRUCBUS[21]; FETCH = PHASEFFBUS[0]; ADDR = PHASEFFBUS[1]; EXEC = PHASEFFBUS[2];
  //   INTR = PHASEFFBUS[3]; PSWSTART = PSW[0]; PSWZ = PSW[1]; PSWN = PSW[2]; PSWV = PSW[3]; PSWC = PSW[4];
  //   PSWI = PSW[5]; rst = in_1

  // Notes on the sheet:
  //   Operaciona jedinica
  //   Y
endmodule

module INTR (
  input  in_1,
  input  in_2,
  input  in_3,
  input  [3:0] PHASEFFBUS,
  input  [21:0] INSTRUCBUS,
  input  [7:0] PSW,
  input  [7:0] intr,
  output [15:0] ADDIVTP,
  output [2:0] UEXT1__0,
  output inta,
  output [14:0] CMEMBUS,
  output [7:0] CFFBUS,
  output [8:0] CREGBUS,
  output rdMEM,
  output wrMEM
);

  wire and_2_out, and_3_out, and_4_out, brcnd, brnotfcbus, brnotintr, brnotprekid, bruncnd, BS0, BS1, clINTR,
       incMAR, incPC, ISELECT, ldB7__0, ldB15__8, ldMAR, ldMDR, ldPC, not_1_out, not_2_out, not_3_out,
       or_1_out, prekid, reg8_inc_ld_1_p5, reg8_inc_ld_1_p6, SAS0, SAS1, sMAR, sMDR, stFETCH, wrMEM_t;
  wire [2:0] CC;
  wire [3:0] adresa;
  wire [3:1] IVD;
  wire [7:0] BA, reg8_inc_ld_1_p4;
  wire [11:11] rom_intr_1_out_3;
  wire [15:0] IVTP15__0;

  and and_1 (prekid, or_1_out, PSW[5], not_2_out);
  not not_1 (not_1_out, in_1);
  // REG16_LD reg16_ld_1: pin names not known; wires that end beside it: in_2, not_1_out, IVTP15__0
  not not_2 (not_2_out, INSTRUCBUS[0]);
  not not_3 (not_3_out, in_1);
  or or_1 (or_1_out, intr[7], intr[6], intr[5], intr[4], intr[3], intr[2], intr[1], intr[0]);
  // REG8_INC_LD reg8_inc_ld_1: pin names not known; wires that end beside it: in_2, not_3_out, BA, reg8_inc_ld_1_p4, reg8_inc_ld_1_p5, reg8_inc_ld_1_p6
  not not_4 (reg8_inc_ld_1_p6, reg8_inc_ld_1_p5);
  or or_2 (reg8_inc_ld_1_p5, bruncnd, brcnd);
  ROM_INTR rom_intr_1 (
    .ADRESA(reg8_inc_ld_1_p4), .CS(1'b1),
    .out_3({SAS0, SAS1, ldMAR, ldMDR, ldPC, incPC, sMDR, wrMEM_t, BS0, BS1, inta, ISELECT, sMAR, incMAR, ldB15__8, ldB7__0, stFETCH, clINTR, rom_intr_1_out_3[11], CC, BA}));
  // CD8 cd8_1: pin names not known; wires that end beside it: intr[7], intr[6], intr[5], intr[4], intr[3], intr[2], intr[1], intr[0], 1'b1, UEXT1__0[2], UEXT1__0[1], UEXT1__0[0]
  // REG3_LD reg3_ld_1: pin names not known; wires that end beside it: in_2, UEXT1__0, IVD, inta
  // DC3_8 dc3_8_1: pin names not known; wires that end beside it: CC, 1'b1, bruncnd, brnotintr, brnotprekid, brnotfcbus
  // ADD16 add16_1: pin names not known; wires that end beside it: {{12{1'b0}}, IVD, 1'b0}, ADDIVTP, IVTP15__0, 1'b0
  and and_2 (and_2_out, ~PHASEFFBUS[3], brnotintr);  // AND_Gate
  and and_3 (and_3_out, ~prekid, brnotprekid);  // AND_Gate
  and and_4 (and_4_out, ~in_3, brnotfcbus);  // AND_Gate
  or or_3 (brcnd, and_2_out, and_3_out, and_4_out);
  // MP4_4b mp4_4b_1: pin names not known; wires that end beside it: SAS1, SAS0, 4'b0000, 4'b0001, adresa, 4'b0010, 1'b1
  assign CMEMBUS[0] = ldMAR ? 1'b1 : 1'bz;  // Controlled_Buffer controlled_buffer_1
  assign CMEMBUS[1] = incMAR ? 1'b1 : 1'bz;  // Controlled_Buffer controlled_buffer_2
  assign CMEMBUS[2] = ldMDR ? 1'b1 : 1'bz;  // Controlled_Buffer controlled_buffer_3
  assign CMEMBUS[3] = ldPC ? 1'b1 : 1'bz;  // Controlled_Buffer controlled_buffer_4
  assign CMEMBUS[9] = sMAR ? 1'b1 : 1'bz;  // Controlled_Buffer controlled_buffer_5
  assign CMEMBUS[10] = sMDR ? 1'b1 : 1'bz;  // Controlled_Buffer controlled_buffer_6
  assign CMEMBUS[11] = ldB15__8 ? 1'b1 : 1'bz;  // Controlled_Buffer controlled_buffer_7
  assign CMEMBUS[12] = ldB7__0 ? 1'b1 : 1'bz;  // Controlled_Buffer controlled_buffer_8
  assign CMEMBUS[13] = BS1 ? 1'b1 : 1'bz;  // Controlled_Buffer controlled_buffer_9
  assign CMEMBUS[14] = BS0 ? 1'b1 : 1'bz;  // Controlled_Buffer controlled_buffer_10
  assign CFFBUS[7] = clINTR ? 1'b1 : 1'bz;  // Controlled_Buffer controlled_buffer_11
  assign CMEMBUS[8:5] = PHASEFFBUS[3] ? adresa : 4'bz;  // Controlled_Buffer controlled_buffer_12
  assign CFFBUS[0] = stFETCH ? 1'b1 : 1'bz;  // Controlled_Buffer controlled_buffer_13
  assign CREGBUS[8] = ISELECT ? 1'b1 : 1'bz;  // Controlled_Buffer controlled_buffer_14
  assign CMEMBUS[4] = incPC ? 1'b1 : 1'bz;  // Controlled_Buffer controlled_buffer_15
  assign wrMEM = wrMEM_t ? 1'b1 : 1'bz;  // Controlled_Buffer controlled_buffer_16

  // Other names for the same wires on the sheet: ldBR = inta; ADDIVTP15__0[15:0] = ADDIVTP; CLK = in_2; FCBUS = in_3;
  //   HALT = INSTRUCBUS[0]; RTS = INSTRUCBUS[1]; RTI = INSTRUCBUS[2]; INTE = INSTRUCBUS[3]; INTD = INSTRUCBUS[4];
  //   ROL = INSTRUCBUS[5]; PUSH = INSTRUCBUS[6]; POP = INSTRUCBUS[7]; BLEQ = INSTRUCBUS[8]; BNVF = INSTRUCBUS[9];
  //   BLSSU = INSTRUCBUS[10]; BOVF = INSTRUCBUS[11]; JEQL = INSTRUCBUS[12]; LOOPGRT = INSTRUCBUS[13];
  //   BR = INSTRUCBUS[14]; JMP = INSTRUCBUS[15]; JSR = INSTRUCBUS[16]; LD = INSTRUCBUS[17]; ST = INSTRUCBUS[18];
  //   ADD = INSTRUCBUS[19]; NOT = INSTRUCBUS[20]; MUL = INSTRUCBUS[21]; intr7__0[7:0] = intr; FETCH = PHASEFFBUS[0];
  //   ADDR = PHASEFFBUS[1]; EXEC = PHASEFFBUS[2]; INTR_t = PHASEFFBUS[3]; PSWSTART = PSW[0]; PSWZ = PSW[1];
  //   PSWN = PSW[2]; PSWV = PSW[3]; PSWC = PSW[4]; PSWI = PSW[5]; rst = in_1; UEXT2__0[2:0] = UEXT1__0

  // Notes on the sheet:
  //   Operaciona jedinica
  //   Upravljacka jedinica
endmodule

module RAM (
  input  [15:0] in_1,
  input  in_2,
  input  [7:0] in_3,
  input  in_4,
  input  in_5,
  input  in_6,
  output [7:0] out_7,
  output out_8
);

  wire and_1_out, and_2_out, CNT0, fc, LDCNT, not_1_out, notCNT0, or_1_out, reg4_ld_sl_sr_1_p6, rsff_2_p4,
       rsff_2_p5, rsff_3_p4, sl;
  wire [3:0] CNT, LFSR;

  // RSFF rsff_1: pin names not known; wires that end beside it: 1'b0, in_2, in_6, sl
  or or_1 (or_1_out, in_4, in_5);
  // REG4_LD_SL_SR reg4_ld_sl_sr_1: pin names not known; wires that end beside it: 1'b0, 1'b0, in_2, 4'b1111, LFSR, reg4_ld_sl_sr_1_p6, sl, in_6
  // RisingEdge risingedge_1: pin names not known; wires that end beside it: or_1_out, in_2, LDCNT
  // MEM64Kx8 mem64kx8_1: pin names not known; wires that end beside it: in_1, 1'b1, in_2, in_3, out_7, in_4
  xor xor_1 (reg4_ld_sl_sr_1_p6, LFSR[2], LFSR[3]);
  and and_1 (and_1_out, CNT0, not_1_out);
  not not_1 (not_1_out, LDCNT);
  // RSFF rsff_2: pin names not known; wires that end beside it: and_1_out, in_2, LDCNT, rsff_2_p4, rsff_2_p5
  not not_2 (rsff_2_p4, in_6);
  and and_2 (and_2_out, rsff_2_p5, CNT0);
  // REG4m_DEC_LD reg4m_dec_ld_1: pin names not known; wires that end beside it: in_2, LFSR, CNT, LDCNT, notCNT0, notCNT0
  or or_2 (notCNT0, CNT[0], CNT[1], CNT[2], CNT[3]);
  // RSFF rsff_3: pin names not known; wires that end beside it: fc, in_2, and_2_out, rsff_3_p4, fc
  not not_3 (rsff_3_p4, in_6);
  not not_4 (CNT0, notCNT0);

  assign out_8 = 1'b1;

  // Other names for the same wires on the sheet: ADR[15:0] = in_1; CLK = in_2; DIN[7:0] = in_3; DOUT[7:0] = out_7;
  //   RDMEM = in_5; rst = in_6; WRMEM = in_4

  // Notes on the sheet:
  //   Random broj predstavlja vreme pristupa memoriji
  //   Brojac za generisanje random broja 
  //   Jedinica za generisanje function complete (fc) signala
  //   Brojac za dekrementiranje random broja
endmodule
